// Digital circuit Add_1bit.dig as structural Verilog
module Add_1bit (
  input  Ci,
  input  Bi,
  input  Ai,
  output Zi,
  output Ci_plus_1
);

  wire INVERSEUR_pin2, INVERSEUR_pin4, INVERSEUR_pin6, INVERSEUR_pin8, INVERSEUR_pin9, NAND2_pin3,
       NAND2_pin6, NAND2_pin8;

  _7400 NAND2 (
    .pin1(Ai), .pin2(Bi), .pin3(NAND2_pin3), .pin4(Ai), .pin5(Ci), .pin6(NAND2_pin6), .pin7(1'b0),
    .pin8(NAND2_pin8), .pin9(Bi), .pin10(Ci), .pin12(1'b0), .pin13(1'b0), .pin14(1'b1));  // open: pin11
  _7404 INVERSEUR (
    .pin1(Ai), .pin2(INVERSEUR_pin2), .pin3(Bi), .pin4(INVERSEUR_pin4), .pin5(Ci), .pin6(INVERSEUR_pin6),
    .pin7(1'b0), .pin8(INVERSEUR_pin8), .pin9(INVERSEUR_pin9), .pin11(1'b0), .pin13(1'b0), .pin14(1'b1));  // open: pin10, pin12
  _7410 NAND3 (
    .pin1(NAND2_pin3), .pin2(NAND2_pin6), .pin3(1'b0), .pin4(1'b0), .pin5(1'b0), .pin7(1'b0), .pin9(1'b0),
    .pin10(1'b0), .pin11(1'b0), .pin12(Ci_plus_1), .pin13(NAND2_pin8), .pin14(1'b1));  // open: pin6, pin8
  _7451 _7451_1 (
    .pin1(1'b0), .pin2(Ai), .pin3(Bi), .pin4(INVERSEUR_pin2), .pin5(INVERSEUR_pin4), .pin6(INVERSEUR_pin9),
    .pin7(1'b0), .pin9(1'b0), .pin10(1'b0), .pin11(1'b0), .pin12(1'b0), .pin13(1'b0), .pin14(1'b1));  // open: pin8
  _7451 _7451_2 (
    .pin1(1'b0), .pin2(INVERSEUR_pin9), .pin3(Ci), .pin4(INVERSEUR_pin8), .pin5(INVERSEUR_pin6), .pin6(Zi),
    .pin7(1'b0), .pin9(1'b0), .pin10(1'b0), .pin11(1'b0), .pin12(1'b0), .pin13(1'b0), .pin14(1'b1));  // open: pin8
  LED led_1 (.in(Ci_plus_1));
  LED led_2 (.in(Zi));
endmodule

/* Test case:
Ai Bi Ci Zi Ci+1
0 0 0 0 0
0 0 1 1 0
0 1 0 1 0
0 1 1 0 1
1 0 0 1 0
1 0 1 0 1
1 1 0 0 1
1 1 1 1 1
*/
