// Digital circuit Add_4bits.dig as structural Verilog
module Add_4bits (
  input  Ai,
  input  Bi,
  input  Ai_plus_1,
  input  Ai_plus_2,
  input  Ai_plus_3,
  input  Bi_plus_1,
  input  Bi_plus_2,
  input  Bi_plus_3,
  input  Ci,
  output Zi,
  output Zi_plus_1,
  output Zi_plus_2,
  output Zi_plus_3,
  output Ci_plus_1,
  output Ci_plus_2,
  output Ci_plus_3,
  output Ci_plus_4
);

  Add_1bit add_1bit_1 (.Ci_plus_1(Bi_plus_1), .Zi(Zi), .Ai(Ai), .Bi(Bi), .Ci(Ci));
  Add_1bit add_1bit_2 (.Ci_plus_1(Ci_plus_2), .Zi(Zi_plus_1), .Ai(Ai_plus_1), .Bi(Bi_plus_1), .Ci(Bi_plus_1));
  Add_1bit add_1bit_3 (.Ci_plus_1(Ci_plus_3), .Zi(Zi_plus_2), .Ai(Ai_plus_2), .Bi(Bi_plus_2), .Ci(Ci_plus_2));
  Add_1bit add_1bit_4 (.Ci_plus_1(Ci_plus_4), .Zi(Zi_plus_3), .Ai(Ai_plus_3), .Bi(Bi_plus_3), .Ci(Ci_plus_3));

  assign Ci_plus_1 = Bi_plus_1;
endmodule

/* Test case:
Ai+3 Ai+2 Ai+1 Ai Bi+3 Bi+2 Bi+1 Bi Ci Zi+3 Zi+2 Zi+1 Zi Ci+4 Ci+3 Ci+2 Ci+1
0 0 0 1 1 0 1 1 0 1 1 0 0 0 0 1 1
1 0 0 0 1 0 1 1 1 0 1 0 0 1 0 1 1
1 1 0 0 1 0 0 1 0 0 1 0 1 1 0 0 0
0 0 0 1 1 0 1 1 0 1 1 0 0 0 0 1 1
*/
