// Digital circuit ComposantsTP.dig as structural Verilog
module ComposantsTP (
  input  Ci,
  input  Bi,
  input  Ai,
  output Zi,
  output Ci_plus_1
);

  wire INVERSEUR_pin2, INVERSEUR_pin4, INVERSEUR_pin6, INVERSEUR_pin12, INVERSEUR_pin13;

  // _7400 NAND2: pin names not known; wires that end beside it: 1'b0, 1'b1, 1'b0, 1'b0
  _7404 INVERSEUR (
    .pin1(Ai), .pin2(INVERSEUR_pin2), .pin3(Bi), .pin4(INVERSEUR_pin4), .pin5(Ci), .pin6(INVERSEUR_pin6),
    .pin7(1'b0), .pin9(1'b0), .pin11(1'b0), .pin12(INVERSEUR_pin12), .pin13(INVERSEUR_pin13), .pin14(1'b1));  // open: pin8, pin10
  _7410 NAND3 (
    .pin3(1'b0), .pin4(1'b0), .pin5(1'b0), .pin7(1'b0), .pin9(1'b0), .pin10(1'b0), .pin11(1'b0), .pin14(1'b1));  // open: pin1, pin2, pin6, pin8, pin12, pin13
  _7451 _7451_1 (
    .pin1(Ai), .pin2(INVERSEUR_pin13), .pin3(Ci), .pin4(INVERSEUR_pin12), .pin5(INVERSEUR_pin6), .pin7(1'b0),
    .pin8(INVERSEUR_pin13), .pin9(1'b1), .pin10(Bi), .pin11(INVERSEUR_pin2), .pin12(1'b1),
    .pin13(INVERSEUR_pin4), .pin14(1'b1));  // open: pin6
  LED led_1 (.in(Ci_plus_1));
  LED led_2 (.in(Zi));
endmodule
