// Digital circuit ExComposant74.dig as structural Verilog
module ExComposant74 (
  input  A,
  input  B,
  input  C,
  output Y
);

  _7410 NAND3 (
    .pin1(A), .pin2(B), .pin3(1'b0), .pin4(1'b0), .pin5(1'b0), .pin7(1'b0), .pin9(1'b0), .pin10(1'b0),
    .pin11(1'b0), .pin12(Y), .pin13(C), .pin14(1'b1));  // open: pin6, pin8
  LED led_1 (.in(Y));
endmodule

/* Test case:
A B C Y
0 0 0 1
0 0 1 1
0 1 0 1
0 1 1 1
1 0 0 1
1 0 1 1
1 1 0 1
1 1 1 0
*/
