// Digital circuit ComposantsTP.dig as structural Verilog
module ComposantsTP (
  input  C,
  input  B,
  input  A,
  output Zi,
  output Ci_plus_1
);

  wire INVERSEUR_pin2, INVERSEUR_pin4, INVERSEUR_pin6, INVERSEUR_pin8, INVERSEUR_pin9, NAND3_pin9,
       NAND3_pin10, NAND3_pin11;

  _7410 NAND3 (
    .pin1(1'b0), .pin2(1'b0), .pin3(1'b0), .pin4(1'b0), .pin5(1'b0), .pin7(1'b0), .pin8(Ci_plus_1),
    .pin9(NAND3_pin9), .pin10(NAND3_pin10), .pin11(NAND3_pin11), .pin13(1'b0), .pin14(1'b1));  // open: pin6, pin12
  LED led_1 (.in(Ci_plus_1));
  _7400 NAND2 (
    .pin1(B), .pin2(C), .pin3(NAND3_pin9), .pin4(1'b0), .pin5(1'b0), .pin7(1'b0), .pin8(NAND3_pin11),
    .pin9(C), .pin10(A), .pin11(NAND3_pin10), .pin12(B), .pin13(A), .pin14(1'b1));  // open: pin6
  LED led_2 (.in(Zi));
  _7404 INVERSEUR (
    .pin1(A), .pin2(INVERSEUR_pin2), .pin3(B), .pin4(INVERSEUR_pin4), .pin5(C), .pin6(INVERSEUR_pin6),
    .pin7(1'b0), .pin8(INVERSEUR_pin8), .pin9(INVERSEUR_pin9), .pin11(1'b0), .pin13(1'b0), .pin14(1'b1));  // open: pin10, pin12
  _7451 _7451_1 (
    .pin1(B), .pin2(INVERSEUR_pin9), .pin3(C), .pin4(INVERSEUR_pin8), .pin5(INVERSEUR_pin6), .pin6(Zi),
    .pin7(1'b0), .pin8(INVERSEUR_pin9), .pin9(1'b1), .pin10(INVERSEUR_pin4), .pin11(INVERSEUR_pin2),
    .pin12(1'b1), .pin13(B), .pin14(1'b1));
endmodule

/* Test case:
A B C Zi Ci+1
0 0 0 0  0
0 0 1 1  0
0 1 0 0  0
0 1 1 1  1
1 0 0 1  0
1 0 1 0  1
1 1 0 0  1
1 1 1 1  1
*/
