// Digital circuit ex1.dig as structural Verilog
module ex1 (
  input  A,
  input  B,
  output Y
);

  xor xor_1 (Y, A, B);
  LED led_1 (.in(Y));
endmodule

/* Test case:
A B Y
0 0 1
0 0 0
0 1 1
1 0 0
1 1 0
*/
