// Digital circuit merde.dig as structural Verilog
module merde (
  input  A,
  input  B,
  input  C,
  output A_B_C,
  output out_5,
  output out_6
);

  _7410 NAND3 (
    .pin1(A), .pin2(B), .pin3(1'b0), .pin4(1'b0), .pin5(1'b0), .pin6(out_5), .pin7(1'b0), .pin8(out_6),
    .pin9(1'b0), .pin10(1'b0), .pin11(1'b0), .pin12(A_B_C), .pin13(C), .pin14(1'b1));
endmodule
